// Logisim project 1byte_BCD_adder_subt_rkb.circ as structural Verilog: 1 circuit, main circuit main
module main (
  input  in_1,
  input  [3:0] in_2,
  input  [3:0] in_3,
  input  [3:0] in_4,
  input  [3:0] in_5,
  input  [3:0] in_6,
  input  [3:0] in_7,
  input  [3:0] in_8,
  input  [3:0] in_9,
  input  [3:0] in_10,
  input  [3:0] in_11,
  input  [3:0] in_12,
  input  [3:0] in_13,
  output [3:0] out_14,
  output [3:0] out_15,
  output out_16,
  output out_17,
  output out_18,
  output out_19,
  output [3:0] out_20,
  output [3:0] out_21,
  output [3:0] out_22,
  output [3:0] out_23
);

  wire add, adder_1_cout, adder_5_cout, and_1_out, and_2_out, and_3_out, and_4_out, sub;
  wire [3:0] adder_1_out, adder_2_out, adder_4_out, adder_5_out, controlled_buffer_1_out,
       controlled_buffer_3_out, xor_1_out, xor_2_out, xor_3_out, xor_4_out;

  Decoder decoder_1 (.out0(add), .out1(sub), .sel(in_1));  // open: en
  and and_1 (and_1_out, adder_1_out[2], adder_1_out[3]);
  assign controlled_buffer_1_out = add ? in_6 : 4'bz;  // Controlled_Buffer controlled_buffer_1
  and and_2 (and_2_out, adder_1_out[1], adder_1_out[3]);
  assign xor_1_out = in_6 ^ in_10;  // XOR_Gate xor_1, 4 bits wide
  Adder #(.width(4)) adder_1 (
    .a(in_3), .b(controlled_buffer_1_out), .out(adder_1_out), .cin(out_18), .cout(adder_1_cout));
  or or_1 (out_19, and_2_out, and_1_out, adder_1_cout);
  assign controlled_buffer_1_out = sub ? adder_2_out : 4'bz;  // Controlled_Buffer controlled_buffer_2
  Adder #(.width(4)) adder_2 (.a(xor_1_out), .b(in_12), .out(adder_2_out));  // open: cin, cout
  Adder #(.width(4)) adder_3 (
    .a(adder_1_out), .b({1'b0, {2{out_19}}, 1'b0}), .out(out_14), .cout(out_16));  // open: cin
  assign controlled_buffer_3_out = add ? in_7 : 4'bz;  // Controlled_Buffer controlled_buffer_3
  and and_3 (and_3_out, adder_5_out[2], adder_5_out[3]);
  assign xor_2_out = in_7 ^ in_11;  // XOR_Gate xor_2, 4 bits wide
  and and_4 (and_4_out, adder_5_out[1], adder_5_out[3]);
  assign controlled_buffer_3_out = sub ? adder_4_out : 4'bz;  // Controlled_Buffer controlled_buffer_4
  Adder #(.width(4)) adder_4 (.a(xor_2_out), .b(in_13), .out(adder_4_out));  // open: cin, cout
  Adder #(.width(4)) adder_5 (
    .a(in_2), .b(controlled_buffer_3_out), .out(adder_5_out), .cout(adder_5_cout));  // open: cin
  or or_2 (out_18, and_4_out, and_3_out, adder_5_cout);
  Adder #(.width(4)) adder_6 (
    .a(adder_5_out), .b({1'b0, {2{out_18}}, 1'b0}), .out(out_15), .cout(out_17));  // open: cin
  assign xor_3_out = out_14 ^ in_5;  // XOR_Gate xor_3, 4 bits wide
  Adder #(.width(4)) adder_7 (.a(xor_3_out), .b(in_9), .out(out_22));  // open: cin, cout
  assign xor_4_out = out_15 ^ in_4;  // XOR_Gate xor_4, 4 bits wide
  Adder #(.width(4)) adder_8 (.a(xor_4_out), .b(in_8), .out(out_23));  // open: cin, cout

  assign out_20 = out_15;
  assign out_21 = out_14;

  // Other names for the same wires on the sheet: carryStage1 = out_18
endmodule
