// Logisim project 81_using_21.circ as structural Verilog: 1 circuit, main circuit main
module main (
  input  I0,
  input  a,
  input  b,
  input  c,
  input  in_5,
  input  in_6,
  input  in_7,
  input  in_8,
  input  in_9,
  input  in_10,
  input  I7,
  output O_P
);

  wire multiplexer_1_out, multiplexer_2_out, multiplexer_3_out, multiplexer_4_out, multiplexer_5_out,
       multiplexer_6_out;

  Multiplexer multiplexer_1 (.in0(I0), .in1(in_5), .out(multiplexer_1_out), .sel(c));  // open: en
  Multiplexer multiplexer_2 (.in0(in_6), .in1(in_7), .out(multiplexer_2_out), .sel(c));  // open: en
  Multiplexer multiplexer_3 (.in0(in_8), .in1(in_9), .out(multiplexer_3_out), .sel(c));  // open: en
  Multiplexer multiplexer_4 (.in0(in_10), .in1(I7), .out(multiplexer_4_out), .sel(c));  // open: en
  Multiplexer multiplexer_5 (
    .in0(multiplexer_1_out), .in1(multiplexer_2_out), .out(multiplexer_5_out), .sel(b));  // open: en
  Multiplexer multiplexer_6 (
    .in0(multiplexer_3_out), .in1(multiplexer_4_out), .out(multiplexer_6_out), .sel(b));  // open: en
  Multiplexer multiplexer_7 (.in0(multiplexer_5_out), .in1(multiplexer_6_out), .out(O_P), .sel(a));  // open: en
endmodule
