// Logisim project 81_using_21_4.circ as structural Verilog: 1 circuit, main circuit main
module main (
  input  in_1,
  input  in_2,
  input  in_3,
  input  in_4,
  input  in_5,
  input  in_6,
  input  [1:0] c1_c2,
  input  in_8,
  input  in_9,
  input  in_10,
  output out_11
);

  wire decoder_1_out0, decoder_1_out1, decoder_1_out2, decoder_1_out3, multiplexer_1_out, multiplexer_2_out,
       multiplexer_3_out, multiplexer_4_out;

  Decoder #(.select(2)) decoder_1 (
    .out0(decoder_1_out0), .out1(decoder_1_out1), .out2(decoder_1_out2), .out3(decoder_1_out3), .sel(c1_c2),
    .en(1'b1));
  Multiplexer multiplexer_1 (.in0(in_1), .in1(in_2), .out(multiplexer_1_out), .sel(decoder_1_out0), .en(in_10));
  Multiplexer multiplexer_2 (.in0(in_3), .in1(in_4), .out(multiplexer_2_out), .sel(decoder_1_out1), .en(in_10));
  Multiplexer multiplexer_3 (.in0(in_5), .in1(in_6), .out(multiplexer_3_out), .sel(decoder_1_out2), .en(in_10));
  Multiplexer multiplexer_4 (.in0(in_8), .in1(in_9), .out(multiplexer_4_out), .sel(decoder_1_out3), .en(in_10));
  or or_1 (out_11, multiplexer_1_out, multiplexer_2_out, multiplexer_3_out, multiplexer_4_out);
endmodule
