// Logisim project Calculator-Display.circ as structural Verilog: 1 circuit, main circuit main
module main (
);

  wire _0, _1, _2, _3, _4, _5, _6, _7, _8, _9, and_1_out, and_2_out, and_3_out, and_4_out, and_5_out,
       and_6_out, and_7_out, and_8_out, and_9_out, and_10_out, and_11_out, and_12_out, and_13_out,
       and_14_out, and_15_out, and_16_out, and_17_out, and_18_out, and_19_out, and_20_out, and_21_out,
       and_22_out, and_23_out, and_24_out, Clear, K, not_1_out, not_2_out, not_3_out, not_4_out, not_5_out,
       not_6_out, not_7_out, not_8_out, not_9_out, not_10_out, not_11_out, not_12_out, not_13_out,
       not_14_out, not_15_out, not_16_out, not_17_out, not_18_out, not_19_out, not_20_out, not_21_out,
       not_22_out, not_23_out, not_24_out, not_25_out, not_26_out, not_27_out, not_28_out, not_29_out,
       not_30_out, or_1_out, or_2_out, or_3_out, or_4_out, or_5_out, or_6_out, or_7_out, or_8_out, or_9_out,
       or_10_out, or_11_out, or_12_out, or_13_out, or_14_out, or_15_out, or_16_out, or_17_out, or_18_out,
       or_19_out, or_20_out, or_21_out, or_22_out, or_23_out, or_24_out, or_25_out, or_26_out, or_29_out,
       or_30_out, or_31_out, or_32_out, or_33_out, or_34_out, or_35_out, or_36_out, or_37_out, or_38_out,
       or_39_out, T1, T2, T3, T3_prime_T4_prime, T4;
  wire [0:0] Tens;
  wire [3:0] A1, A2, A3, A4, A5, A6, A7, A8, A9, A10, A11, A12, Units;

  not not_1 (not_1_out, T4);
  not not_2 (not_2_out, T3);
  Button u__1 (.out(_1));
  Button u__4 (.out(_4));
  Button u__7 (.out(_7));
  or or_1 (or_1_out, _0, _1, _2, _3, _4, _5, _6, _7, _8, _9);
  or or_2 (or_2_out, not_1_out, not_2_out);
  or or_3 (or_3_out, _0, _1, _2, _3, _4, _5, _6, _7);
  or or_4 (or_4_out, _8, _9);
  or or_5 (or_5_out, _0, _1, _2, _3, _8, _9);
  or or_6 (or_6_out, _4, _5, _6, _7);
  or or_7 (or_7_out, _0, _1, _4, _5, _8, _9);
  or or_8 (or_8_out, _2, _3, _6, _7);
  or or_9 (or_9_out, _0, _2, _4, _6, _8);
  or or_10 (or_10_out, _1, _3, _5, _7, _9);
  and and_1 (and_1_out, or_11_out, or_17_out);
  or or_11 (or_11_out, _0, _6, _1, _7, _2, _3, _8, _4, _9, _5);
  or or_12 (or_12_out, _0, _6, _1, _7, _2, _3, _8, _4, _9, _5);
  or or_13 (or_13_out, _0, _6, _1, _7, _2, _3, _8, _4, _9, _5);
  or or_14 (or_14_out, _0, _6, _1, _7, _2, _3, _8, _4, _9, _5);
  or or_15 (or_15_out, _0, _6, _1, _7, _2, _3, _8, _4, _9, _5);
  or or_16 (or_16_out, _0, _6, _1, _7, _2, _3, _8, _4, _9, _5);
  Button u__2 (.out(_2));
  Button u__5 (.out(_5));
  Button u__8 (.out(_8));
  Button u__0 (.out(_0));
  and and_2 (and_2_out, or_1_out, or_2_out);
  Adder #(.width(4)) adder_1 (
    .a({1'b0, {2{K}}, 1'b0}), .b({T4, T3, T2, T1}), .out(Units), .cout(Tens[0]));  // open: cin
  not not_3 (not_3_out, or_3_out);
  and and_3 (and_3_out, not_3_out, or_4_out);
  not not_4 (not_4_out, or_5_out);
  not not_5 (not_5_out, or_7_out);
  not not_6 (not_6_out, or_9_out);
  and and_4 (and_4_out, not_6_out, or_10_out);
  D_Flip_Flop d_ff_1 (.clk(and_1_out), .D(A1[0]), .Q(A2[0]), .reset(Clear));  // open: Qn, preset, en
  D_Flip_Flop d_ff_2 (.clk(and_1_out), .D(A1[1]), .Q(A2[1]), .reset(Clear));  // open: Qn, preset, en
  D_Flip_Flop d_ff_3 (.clk(and_1_out), .D(A1[2]), .Q(A2[2]), .reset(Clear));  // open: Qn, preset, en
  D_Flip_Flop d_ff_4 (.clk(and_1_out), .D(A1[3]), .Q(A2[3]), .reset(Clear));  // open: Qn, preset, en
  or or_17 (or_17_out, not_8_out, not_7_out);
  not not_7 (not_7_out, T4);
  not not_8 (not_8_out, T3);
  D_Flip_Flop d_ff_5 (.clk(and_5_out), .D(A3[0]), .Q(A4[0]), .reset(Clear));  // open: Qn, preset, en
  D_Flip_Flop d_ff_6 (.clk(and_5_out), .D(A3[1]), .Q(A4[1]), .reset(Clear));  // open: Qn, preset, en
  D_Flip_Flop d_ff_7 (.clk(and_5_out), .D(A3[2]), .Q(A4[2]), .reset(Clear));  // open: Qn, preset, en
  D_Flip_Flop d_ff_8 (.clk(and_5_out), .D(A3[3]), .Q(A4[3]), .reset(Clear));  // open: Qn, preset, en
  and and_5 (and_5_out, or_12_out, or_18_out);
  or or_18 (or_18_out, not_9_out, not_10_out);
  not not_9 (not_9_out, T3);
  not not_10 (not_10_out, T4);
  D_Flip_Flop d_ff_9 (.clk(and_6_out), .D(A5[0]), .Q(A6[0]), .reset(Clear));  // open: Qn, preset, en
  D_Flip_Flop d_ff_10 (.clk(and_6_out), .D(A5[1]), .Q(A6[1]), .reset(Clear));  // open: Qn, preset, en
  D_Flip_Flop d_ff_11 (.clk(and_6_out), .D(A5[2]), .Q(A6[2]), .reset(Clear));  // open: Qn, preset, en
  D_Flip_Flop d_ff_12 (.clk(and_6_out), .D(A5[3]), .Q(A6[3]), .reset(Clear));  // open: Qn, preset, en
  and and_6 (and_6_out, or_13_out, or_19_out);
  or or_19 (or_19_out, not_12_out, not_11_out);
  not not_11 (not_11_out, T4);
  not not_12 (not_12_out, T3);
  D_Flip_Flop d_ff_13 (.clk(and_7_out), .D(A7[0]), .Q(A8[0]), .reset(Clear));  // open: Qn, preset, en
  D_Flip_Flop d_ff_14 (.clk(and_7_out), .D(A7[1]), .Q(A8[1]), .reset(Clear));  // open: Qn, preset, en
  D_Flip_Flop d_ff_15 (.clk(and_7_out), .D(A7[2]), .Q(A8[2]), .reset(Clear));  // open: Qn, preset, en
  D_Flip_Flop d_ff_16 (.clk(and_7_out), .D(A7[3]), .Q(A8[3]), .reset(Clear));  // open: Qn, preset, en
  and and_7 (and_7_out, or_14_out, or_20_out);
  or or_20 (or_20_out, not_14_out, not_13_out);
  not not_13 (not_13_out, T4);
  not not_14 (not_14_out, T3);
  D_Flip_Flop d_ff_17 (.clk(and_8_out), .D(A9[0]), .Q(A10[0]), .reset(Clear));  // open: Qn, preset, en
  D_Flip_Flop d_ff_18 (.clk(and_8_out), .D(A9[1]), .Q(A10[1]), .reset(Clear));  // open: Qn, preset, en
  D_Flip_Flop d_ff_19 (.clk(and_8_out), .D(A9[2]), .Q(A10[2]), .reset(Clear));  // open: Qn, preset, en
  D_Flip_Flop d_ff_20 (.clk(and_8_out), .D(A9[3]), .Q(A10[3]), .reset(Clear));  // open: Qn, preset, en
  and and_8 (and_8_out, or_15_out, or_21_out);
  or or_21 (or_21_out, not_15_out, not_16_out);
  not not_15 (not_15_out, T3);
  not not_16 (not_16_out, T4);
  D_Flip_Flop d_ff_21 (.clk(and_9_out), .D(A11[0]), .Q(A12[0]), .reset(Clear));  // open: Qn, preset, en
  D_Flip_Flop d_ff_22 (.clk(and_9_out), .D(A11[1]), .Q(A12[1]), .reset(Clear));  // open: Qn, preset, en
  D_Flip_Flop d_ff_23 (.clk(and_9_out), .D(A11[2]), .Q(A12[2]), .reset(Clear));  // open: Qn, preset, en
  D_Flip_Flop d_ff_24 (.clk(and_9_out), .D(A11[3]), .Q(A12[3]), .reset(Clear));  // open: Qn, preset, en
  and and_9 (and_9_out, or_16_out, or_22_out);
  or or_22 (or_22_out, not_18_out, not_17_out);
  not not_17 (not_17_out, T4);
  not not_18 (not_18_out, T3);
  Button u__3 (.out(_3));
  Button u__6 (.out(_6));
  Button u__9 (.out(_9));
  Button CE (.out(Clear));
  T_Flip_Flop t_ff_1 (.clk(and_2_out), .T(and_10_out), .Q(T4), .reset(Clear));  // open: Qn, preset, en
  and and_10 (and_10_out, T3, and_17_out);
  and and_11 (and_11_out, T3_prime_T4_prime, or_23_out);
  or or_23 (or_23_out, or_4_out, or_3_out);
  and and_12 (and_12_out, T3_prime_T4_prime, or_24_out);
  or or_24 (or_24_out, or_5_out, or_6_out);
  and and_13 (and_13_out, not_4_out, or_6_out);
  and and_14 (and_14_out, T3_prime_T4_prime, or_25_out);
  or or_25 (or_25_out, or_7_out, or_8_out);
  and and_15 (and_15_out, not_5_out, or_8_out);
  and and_16 (and_16_out, T3_prime_T4_prime, or_26_out);
  or or_26 (or_26_out, or_9_out, or_10_out);
  Hex_Digit_Display hex_digit_display_1 (.value({3'b000, Tens[0]}));  // open: dp
  T_Flip_Flop t_ff_2 (.clk(and_2_out), .T(and_17_out), .Q(T3), .reset(Clear));  // open: Qn, preset, en
  and and_17 (and_17_out, T2, T1);
  D_Flip_Flop d_ff_25 (.clk(and_11_out), .D(and_3_out), .Q(A1[3]), .reset(Clear));  // open: Qn, preset, en
  D_Flip_Flop d_ff_26 (.clk(and_12_out), .D(and_13_out), .Q(A1[2]), .reset(Clear));  // open: Qn, preset, en
  D_Flip_Flop d_ff_27 (.clk(and_14_out), .D(and_15_out), .Q(A1[1]), .reset(Clear));  // open: Qn, preset, en
  D_Flip_Flop d_ff_28 (.clk(and_16_out), .D(and_4_out), .Q(A1[0]), .reset(Clear));  // open: Qn, preset, en
  Hex_Digit_Display hex_digit_display_2 (.value(A12));  // open: dp
  Hex_Digit_Display hex_digit_display_3 (.value(A11));  // open: dp
  Hex_Digit_Display hex_digit_display_4 (.value(Units));  // open: dp
  or or_27 (K, and_18_out, and_19_out);
  and and_18 (and_18_out, T4, T3);
  and and_19 (and_19_out, T4, T2);
  Hex_Digit_Display hex_digit_display_5 (.value(A9));  // open: dp
  Hex_Digit_Display hex_digit_display_6 (.value(A10));  // open: dp
  T_Flip_Flop t_ff_3 (.clk(and_2_out), .T(T1), .Q(T2), .reset(Clear));  // open: Qn, preset, en
  not not_19 (not_19_out, T3);
  or or_28 (T3_prime_T4_prime, not_19_out, not_20_out);
  not not_20 (not_20_out, T4);
  or or_29 (or_29_out, _0, _6, _1, _7, _2, _3, _8, _4, _9, _5);
  or or_30 (or_30_out, _0, _6, _1, _7, _2, _3, _8, _4, _9, _5);
  or or_31 (or_31_out, _0, _6, _1, _7, _2, _3, _8, _4, _9, _5);
  or or_32 (or_32_out, _0, _6, _1, _7, _2, _3, _8, _4, _9, _5);
  or or_33 (or_33_out, _0, _6, _1, _7, _2, _3, _8, _4, _9, _5);
  Hex_Digit_Display hex_digit_display_7 (.value(A8));  // open: dp
  Hex_Digit_Display hex_digit_display_8 (.value(A7));  // open: dp
  T_Flip_Flop t_ff_4 (.clk(and_2_out), .T(or_34_out), .Q(T1), .reset(Clear));  // open: Qn, preset, en
  or or_34 (or_34_out, _0, _1, _2, _3, _4, _5, _6, _7, _8, _9);
  D_Flip_Flop d_ff_29 (.clk(and_20_out), .D(A2[0]), .Q(A3[0]), .reset(Clear));  // open: Qn, preset, en
  D_Flip_Flop d_ff_30 (.clk(and_20_out), .D(A2[1]), .Q(A3[1]), .reset(Clear));  // open: Qn, preset, en
  D_Flip_Flop d_ff_31 (.clk(and_20_out), .D(A2[2]), .Q(A3[2]), .reset(Clear));  // open: Qn, preset, en
  D_Flip_Flop d_ff_32 (.clk(and_20_out), .D(A2[3]), .Q(A3[3]), .reset(Clear));  // open: Qn, preset, en
  and and_20 (and_20_out, or_29_out, or_35_out);
  D_Flip_Flop d_ff_33 (.clk(and_21_out), .D(A4[0]), .Q(A5[0]), .reset(Clear));  // open: Qn, preset, en
  D_Flip_Flop d_ff_34 (.clk(and_21_out), .D(A4[1]), .Q(A5[1]), .reset(Clear));  // open: Qn, preset, en
  D_Flip_Flop d_ff_35 (.clk(and_21_out), .D(A4[2]), .Q(A5[2]), .reset(Clear));  // open: Qn, preset, en
  D_Flip_Flop d_ff_36 (.clk(and_21_out), .D(A4[3]), .Q(A5[3]), .reset(Clear));  // open: Qn, preset, en
  and and_21 (and_21_out, or_30_out, or_36_out);
  D_Flip_Flop d_ff_37 (.clk(and_22_out), .D(A6[0]), .Q(A7[0]), .reset(Clear));  // open: Qn, preset, en
  D_Flip_Flop d_ff_38 (.clk(and_22_out), .D(A6[1]), .Q(A7[1]), .reset(Clear));  // open: Qn, preset, en
  D_Flip_Flop d_ff_39 (.clk(and_22_out), .D(A6[2]), .Q(A7[2]), .reset(Clear));  // open: Qn, preset, en
  D_Flip_Flop d_ff_40 (.clk(and_22_out), .D(A6[3]), .Q(A7[3]), .reset(Clear));  // open: Qn, preset, en
  and and_22 (and_22_out, or_31_out, or_37_out);
  Hex_Digit_Display hex_digit_display_9 (.value(A5));  // open: dp
  Hex_Digit_Display hex_digit_display_10 (.value(A6));  // open: dp
  or or_35 (or_35_out, not_22_out, not_21_out);
  not not_21 (not_21_out, T4);
  not not_22 (not_22_out, T3);
  or or_36 (or_36_out, not_24_out, not_23_out);
  not not_23 (not_23_out, T4);
  not not_24 (not_24_out, T3);
  or or_37 (or_37_out, not_25_out, not_26_out);
  not not_25 (not_25_out, T3);
  not not_26 (not_26_out, T4);
  D_Flip_Flop d_ff_41 (.clk(and_23_out), .D(A8[0]), .Q(A9[0]), .reset(Clear));  // open: Qn, preset, en
  D_Flip_Flop d_ff_42 (.clk(and_23_out), .D(A8[1]), .Q(A9[1]), .reset(Clear));  // open: Qn, preset, en
  D_Flip_Flop d_ff_43 (.clk(and_23_out), .D(A8[2]), .Q(A9[2]), .reset(Clear));  // open: Qn, preset, en
  D_Flip_Flop d_ff_44 (.clk(and_23_out), .D(A8[3]), .Q(A9[3]), .reset(Clear));  // open: Qn, preset, en
  and and_23 (and_23_out, or_32_out, or_38_out);
  or or_38 (or_38_out, not_28_out, not_27_out);
  not not_27 (not_27_out, T4);
  not not_28 (not_28_out, T3);
  D_Flip_Flop d_ff_45 (.clk(and_24_out), .D(A10[0]), .Q(A11[0]), .reset(Clear));  // open: Qn, preset, en
  D_Flip_Flop d_ff_46 (.clk(and_24_out), .D(A10[1]), .Q(A11[1]), .reset(Clear));  // open: Qn, preset, en
  D_Flip_Flop d_ff_47 (.clk(and_24_out), .D(A10[2]), .Q(A11[2]), .reset(Clear));  // open: Qn, preset, en
  D_Flip_Flop d_ff_48 (.clk(and_24_out), .D(A10[3]), .Q(A11[3]), .reset(Clear));  // open: Qn, preset, en
  and and_24 (and_24_out, or_33_out, or_39_out);
  or or_39 (or_39_out, not_29_out, not_30_out);
  not not_29 (not_29_out, T3);
  not not_30 (not_30_out, T4);
  Hex_Digit_Display hex_digit_display_11 (.value(A3));  // open: dp
  Hex_Digit_Display hex_digit_display_12 (.value(A4));  // open: dp
  Hex_Digit_Display hex_digit_display_13 (.value(A1));  // open: dp
  Hex_Digit_Display hex_digit_display_14 (.value(A2));  // open: dp

  // Notes on the sheet:
  //    MODULO-12 COUNTER
  //   4 11-bit LEFT SHIFT REGISTERS
  //   Input Buttons
  //   D FLIP-FLOP(TAKES INPUT)
  //   bit 3
  //   bit 2
  //   bit 1
  //   bit 0
  //   T2
  //   T1
  //   DISPLAY
endmodule
