// Logisim project GCD_rkb.circ as structural Verilog: 1 circuit, main circuit main
module main (
  input  [3:0] in_1,
  input  [3:0] in_2,
  input  [3:0] in_3,
  input  [3:0] in_4,
  input  [3:0] in_5,
  input  [3:0] in_6,
  input  [3:0] in_7,
  input  [3:0] in_8,
  input  [3:0] in_9,
  input  [3:0] in_10,
  output [3:0] out_11
);

  wire comparator_1_eq, comparator_2_eq, comparator_3_eq, comparator_4_eq;
  wire [3:0] divider_1_rem, divider_2_rem, divider_3_rem, divider_4_rem, multiplexer_1_out,
       multiplexer_2_out, multiplexer_3_out, multiplexer_4_out;

  Divider #(.width(4)) divider_1 (.a(in_1), .b(in_4), .rem(divider_1_rem));  // open: out, upper
  Divider #(.width(4)) divider_2 (.a(in_4), .b(divider_1_rem), .rem(divider_2_rem));  // open: out, upper
  Divider #(.width(4)) divider_3 (.a(divider_1_rem), .b(divider_2_rem), .rem(divider_3_rem));  // open: out, upper
  Divider #(.width(4)) divider_4 (.a(divider_2_rem), .b(divider_3_rem), .rem(divider_4_rem));  // open: out, upper
  Comparator #(.width(4)) comparator_1 (.a(in_3), .b(divider_1_rem), .eq(comparator_1_eq));  // open: gt, lt
  Comparator #(.width(4)) comparator_2 (.a(in_6), .b(divider_2_rem), .eq(comparator_2_eq));  // open: gt, lt
  Comparator #(.width(4)) comparator_3 (.a(in_8), .b(divider_3_rem), .eq(comparator_3_eq));  // open: gt, lt
  Comparator #(.width(4)) comparator_4 (.a(in_10), .b(divider_4_rem), .eq(comparator_4_eq));  // open: gt, lt
  Multiplexer #(.width(4), .enable("false")) multiplexer_1 (
    .in0(in_2), .in1(in_4), .out(multiplexer_1_out), .sel(comparator_1_eq));
  Multiplexer #(.width(4), .enable("false")) multiplexer_2 (
    .in0(in_5), .in1(divider_1_rem), .out(multiplexer_2_out), .sel(comparator_2_eq));
  Multiplexer #(.width(4), .enable("false")) multiplexer_3 (
    .in0(in_7), .in1(divider_2_rem), .out(multiplexer_3_out), .sel(comparator_3_eq));
  Multiplexer #(.width(4), .enable("false")) multiplexer_4 (
    .in0(in_9), .in1(divider_3_rem), .out(multiplexer_4_out), .sel(comparator_4_eq));
  assign out_11 = multiplexer_1_out | multiplexer_2_out | multiplexer_3_out | multiplexer_4_out;  // OR_Gate or_1, 4 bits wide
endmodule
