// Logisim project MULTIPLIER.circ as structural Verilog: 1 circuit, main circuit main
module main (
  output As
);

  wire _1, adder_1_cout, Bs;
  wire [0:0] e_q;
  wire [3:0] A, adder_1_out, B, controlled_buffer_1_out, Qs, undriven, undriven_2;

  assign controlled_buffer_1_out = _1 ? adder_1_out : 4'bz;  // Controlled_Buffer controlled_buffer_1
  Adder #(.width(4)) adder_1 (.a(B), .b(A), .out(adder_1_out), .cout(adder_1_cout));  // open: cin
  Register #(.width(5)) u_b (.Q({Bs, B}));  // open: D, en, clk, clr
  Register #(.width(5)) q (.Q({Qs, Qs[0]}));  // open: D, en, clk, clr
  Register #(.width(4)) u_a (.D(controlled_buffer_1_out), .Q(A));  // open: en, clk, clr
  Register #(.width(1)) e (.D(adder_1_cout), .Q(e_q[0]));  // open: en, clk, clr
  Comparator #(.width(1)) comparator_1 (.a(1'b1), .b(Qs[3]), .eq(_1));  // open: gt, lt
  Shift_Register #(.width(9)) EAQ (.in({undriven_2, undriven, e_q[0]}));  // open: shift, clk, out, load, clr, d0, q0, d1, q1, d2, q2, d3, q3, d4, q4, d5, q5, d6, q6, d7, q7
  xor xor_1 (As, Bs, Qs[0]);
  // Pins of 1 and 4 bits meet at Qs
endmodule
