// Logisim project ad_sub_inr_decr_rkb.circ as structural Verilog: 1 circuit, main circuit main
module main (
  input  in_1,
  input  in_2,
  input  in_3,
  input  in_4,
  input  [1:0] in_5,
  input  in_6,
  input  in_7,
  input  in_8,
  input  in_9,
  output out_10,
  output out_11,
  output out_12,
  output out_13,
  output out_14
);

  wire adder_2_cout, adder_3_cout, adder_4_cout, multiplexer_1_out, multiplexer_2_out, multiplexer_3_out,
       multiplexer_4_out, not_1_out, not_2_out, not_3_out, not_4_out, not_5_out, not_6_out, not_7_out,
       not_8_out, xor_1_out;

  not not_1 (not_1_out, in_1);
  Multiplexer #(.select(2)) multiplexer_1 (
    .in0(in_1), .in1(not_1_out), .in2(1'b0), .in3(not_2_out), .out(multiplexer_1_out), .sel(in_5));  // open: en
  not not_2 (not_2_out, 1'b0);
  Adder #(.width(1)) adder_1 (.a(multiplexer_1_out), .b(in_6), .out(out_11), .cin(adder_2_cout), .cout(out_14));
  not not_3 (not_3_out, in_2);
  Multiplexer #(.select(2)) multiplexer_2 (
    .in0(in_2), .in1(not_3_out), .in2(1'b0), .in3(not_4_out), .out(multiplexer_2_out), .sel(in_5));  // open: en
  not not_4 (not_4_out, 1'b0);
  Adder #(.width(1)) adder_2 (.a(multiplexer_2_out), .b(in_7), .out(out_12), .cin(adder_3_cout), .cout(adder_2_cout));
  not not_5 (not_5_out, in_3);
  Multiplexer #(.select(2)) multiplexer_3 (
    .in0(in_3), .in1(not_5_out), .in2(1'b0), .in3(not_6_out), .out(multiplexer_3_out), .sel(in_5));  // open: en
  Adder #(.width(1)) adder_3 (.a(multiplexer_3_out), .b(in_8), .out(out_13), .cin(adder_4_cout), .cout(adder_3_cout));
  not not_6 (not_6_out, 1'b0);
  not not_7 (not_7_out, in_4);
  Multiplexer #(.select(2)) multiplexer_4 (
    .in0(in_4), .in1(not_7_out), .in2(1'b0), .in3(not_8_out), .out(multiplexer_4_out), .sel(in_5));  // open: en
  Adder #(.width(1)) adder_4 (.a(multiplexer_4_out), .b(in_9), .out(out_10), .cin(xor_1_out), .cout(adder_4_cout));
  not not_8 (not_8_out, 1'b0);
  xor xor_1 (xor_1_out, in_5[0], in_5[1]);
endmodule
