// Logisim project adder_subtractor_rkb.circ as structural Verilog: 1 circuit, main circuit main
module main (
  input  cs,
  input  a3,
  input  a2,
  input  a1,
  input  a0,
  input  b3,
  input  b2,
  input  b1,
  input  b0,
  output o0,
  output o1,
  output o2,
  output o3,
  output cout
);

  wire adder_2_cout, adder_3_cout, adder_4_cout, xor_1_out, xor_2_out, xor_3_out, xor_4_out;

  xor xor_1 (xor_1_out, b3, cs);
  Adder #(.width(1)) adder_1 (.a(xor_1_out), .b(a3), .out(o3), .cin(adder_2_cout), .cout(cout));
  xor xor_2 (xor_2_out, b2, cs);
  Adder #(.width(1)) adder_2 (.a(xor_2_out), .b(a2), .out(o2), .cin(adder_3_cout), .cout(adder_2_cout));
  xor xor_3 (xor_3_out, b1, cs);
  Adder #(.width(1)) adder_3 (.a(xor_3_out), .b(a1), .out(o1), .cin(adder_4_cout), .cout(adder_3_cout));
  xor xor_4 (xor_4_out, b0, cs);
  Adder #(.width(1)) adder_4 (.a(xor_4_out), .b(a0), .out(o0), .cin(cs), .cout(adder_4_cout));
endmodule
