// Logisim project arith_logic_shift.circ as structural Verilog: 1 circuit, main circuit main
module main (
  input  [3:0] in_1,
  input  [1:0] in_2,
  input  [1:0] in_3,
  input  [3:0] b,
  input  [3:0] a0a1a2a3,
  input  [1:0] in_6,
  input  in_7,
  input  in_8,
  input  [2:0] in_9,
  output out_10,
  output [3:0] out_arit_o0o1o2o3,
  output [3:0] out_logical,
  output out_13,
  output out_14,
  output out_15,
  output out_16
);

  wire A0, A1, A2, A3, adder_2_cout, adder_3_cout, adder_4_cout, arithmatic, clock_1_out, decoder_1_out2,
       decoder_1_out3, logical, multiplexer_1_out, multiplexer_2_out, multiplexer_3_out, multiplexer_4_out,
       multiplexer_5_out, multiplexer_7_out, multiplexer_8_out, multiplexer_9_out, not_1_out, not_2_out,
       not_4_out, not_5_out, not_6_out, not_7_out, not_8_out, not_9_out, shift_operation, xor_2_out;
  wire [3:0] and_1_out, controlled_buffer_1_out, controlled_buffer_2_out, not_3_out, or_1_out, xor_1_out;

  assign controlled_buffer_1_out = logical ? b : 4'bz;  // Controlled_Buffer controlled_buffer_1
  Multiplexer #(.select(2)) multiplexer_1 (
    .in0(in_1[3]), .in1(not_1_out), .in2(1'b0), .in3(not_2_out), .out(multiplexer_1_out), .sel(in_2),
    .en(arithmatic));
  not not_1 (not_1_out, in_1[3]);
  not not_2 (not_2_out, 1'b0);
  Adder #(.width(1)) adder_1 (
    .a(multiplexer_1_out), .b(a0a1a2a3[0]), .out(out_arit_o0o1o2o3[0]), .cin(adder_2_cout), .cout(out_10));
  assign xor_1_out = controlled_buffer_2_out ^ controlled_buffer_1_out;  // XOR_Gate xor_1, 4 bits wide
  assign not_3_out = ~controlled_buffer_2_out;  // NOT_Gate not_3, 4 bits wide
  Multiplexer #(.select(3)) multiplexer_2 (
    .in0(A2), .in1(in_7), .in2(A3), .in3(A3), .in4(A2), .in5(A0), .in6(A3), .in7(A3),
    .out(multiplexer_2_out), .sel(in_9));  // open: en
  D_Flip_Flop d_ff_1 (.clk(clock_1_out), .D(multiplexer_2_out), .Q(out_13));  // open: Qn, preset, en, reset
  assign or_1_out = controlled_buffer_2_out | controlled_buffer_1_out;  // OR_Gate or_1, 4 bits wide
  Multiplexer #(.select(2)) multiplexer_3 (
    .in0(in_1[2]), .in1(not_4_out), .in2(1'b0), .in3(not_5_out), .out(multiplexer_3_out), .sel(in_2),
    .en(arithmatic));
  assign and_1_out = controlled_buffer_2_out & controlled_buffer_1_out;  // AND_Gate and_1, 4 bits wide
  not not_4 (not_4_out, in_1[2]);
  not not_5 (not_5_out, 1'b0);
  Adder #(.width(1)) adder_2 (
    .a(multiplexer_3_out), .b(a0a1a2a3[1]), .out(out_arit_o0o1o2o3[1]), .cin(adder_3_cout),
    .cout(adder_2_cout));
  Multiplexer #(.select(3)) multiplexer_4 (
    .in0(A1), .in1(A3), .in2(A3), .in3(A1), .in4(A1), .in5(A3), .in6(A2), .in7(A2), .out(multiplexer_4_out),
    .sel(in_9));  // open: en
  D_Flip_Flop d_ff_2 (.clk(clock_1_out), .D(multiplexer_4_out), .Q(out_14));  // open: Qn, preset, en, reset
  not not_6 (not_6_out, in_1[1]);
  Multiplexer #(.select(2)) multiplexer_5 (
    .in0(in_1[1]), .in1(not_6_out), .in2(1'b0), .in3(not_7_out), .out(multiplexer_5_out), .sel(in_2),
    .en(arithmatic));
  Adder #(.width(1)) adder_3 (
    .a(multiplexer_5_out), .b(a0a1a2a3[2]), .out(out_arit_o0o1o2o3[2]), .cin(adder_4_cout),
    .cout(adder_3_cout));
  Multiplexer #(.select(2), .width(4)) multiplexer_6 (
    .in0(or_1_out), .in1(and_1_out), .in2(xor_1_out), .in3(not_3_out), .out(out_logical), .sel(in_6));  // open: en
  Multiplexer #(.select(3)) multiplexer_7 (
    .in0(A0), .in1(A2), .in2(A2), .in3(A0), .in4(A0), .in5(A2), .in6(A1), .in7(A1), .out(multiplexer_7_out),
    .sel(in_9));  // open: en
  not not_7 (not_7_out, 1'b0);
  D_Flip_Flop d_ff_3 (.clk(clock_1_out), .D(multiplexer_7_out), .Q(out_15));  // open: Qn, preset, en, reset
  not not_8 (not_8_out, in_1[0]);
  Multiplexer #(.select(2)) multiplexer_8 (
    .in0(in_1[0]), .in1(not_8_out), .in2(1'b0), .in3(not_9_out), .out(multiplexer_8_out), .sel(in_2),
    .en(arithmatic));
  not not_9 (not_9_out, 1'b0);
  Adder #(.width(1)) adder_4 (
    .a(multiplexer_8_out), .b(a0a1a2a3[3]), .out(out_arit_o0o1o2o3[3]), .cin(xor_2_out), .cout(adder_4_cout));
  xor xor_2 (xor_2_out, in_2[0], in_2[1]);
  Multiplexer #(.select(3)) multiplexer_9 (
    .in0(in_8), .in1(A1), .in2(A1), .in3(in_8), .in4(A3), .in5(A1), .in6(A0), .in7(A0),
    .out(multiplexer_9_out), .sel(in_9));  // open: en
  assign controlled_buffer_2_out = logical ? a0a1a2a3 : 4'bz;  // Controlled_Buffer controlled_buffer_2
  Clock clock_1 (.out(clock_1_out));
  D_Flip_Flop d_ff_4 (.clk(clock_1_out), .D(multiplexer_9_out), .Q(out_16));  // open: Qn, preset, en, reset
  Decoder #(.select(2), .enable("false")) decoder_1 (
    .out0(arithmatic), .out1(logical), .out2(decoder_1_out2), .out3(decoder_1_out3), .sel(in_3));
  or or_2 (shift_operation, decoder_1_out2, decoder_1_out3);
  assign A3 = shift_operation ? a0a1a2a3[0] : 1'bz;  // Controlled_Buffer controlled_buffer_3
  assign A2 = shift_operation ? a0a1a2a3[1] : 1'bz;  // Controlled_Buffer controlled_buffer_4
  assign A1 = shift_operation ? a0a1a2a3[2] : 1'bz;  // Controlled_Buffer controlled_buffer_5
  assign A0 = shift_operation ? a0a1a2a3[3] : 1'bz;  // Controlled_Buffer controlled_buffer_6

  // Other names for the same wires on the sheet: b0 = in_1[0]; b1 = in_1[1]; b2 = in_1[2]; b3 = in_1[3]

  // Notes on the sheet:
  //   000:shift left
  //   001:shift right
  //   010:arithmatic shift right
  //   011:arithmatic shift left
  //   100:circular shift left
  //   101:circular shift right
  //   110:nop
  //   111:nop
endmodule
