// Logisim project arithmatic_logical_rkb.circ as structural Verilog: 1 circuit, main circuit main
// a3a2a1a0
module main (
  input  [3:0] in_1,
  input  [1:0] in_2,
  input  [3:0] b,
  input  [3:0] a0a1a2a3,
  input  [1:0] in_5,
  input  in_6,
  output out_7,
  output [3:0] out_arit_o0o1o2o3,
  output [3:0] out_logical
);

  wire adder_2_cout, adder_3_cout, adder_4_cout, arithmatic, logical, multiplexer_1_out, multiplexer_2_out,
       multiplexer_3_out, multiplexer_5_out, not_1_out, not_2_out, not_4_out, not_5_out, not_6_out,
       not_7_out, not_8_out, not_9_out, xor_2_out;
  wire [3:0] and_1_out, controlled_buffer_1_out, controlled_buffer_2_out, not_3_out, or_1_out, xor_1_out;

  assign controlled_buffer_1_out = logical ? b : 4'bz;  // Controlled_Buffer controlled_buffer_1
  Decoder #(.enable("false")) decoder_1 (.out0(arithmatic), .out1(logical), .sel(in_6));
  Multiplexer #(.select(2)) multiplexer_1 (
    .in0(in_1[3]), .in1(not_1_out), .in2(1'b0), .in3(not_2_out), .out(multiplexer_1_out), .sel(in_2),
    .en(arithmatic));
  not not_1 (not_1_out, in_1[3]);
  not not_2 (not_2_out, 1'b0);
  Adder #(.width(1)) adder_1 (
    .a(multiplexer_1_out), .b(a0a1a2a3[0]), .out(out_arit_o0o1o2o3[0]), .cin(adder_2_cout), .cout(out_7));
  assign xor_1_out = controlled_buffer_2_out ^ controlled_buffer_1_out;  // XOR_Gate xor_1, 4 bits wide
  assign not_3_out = ~controlled_buffer_2_out;  // NOT_Gate not_3, 4 bits wide
  assign or_1_out = controlled_buffer_2_out | controlled_buffer_1_out;  // OR_Gate or_1, 4 bits wide
  Multiplexer #(.select(2)) multiplexer_2 (
    .in0(in_1[2]), .in1(not_4_out), .in2(1'b0), .in3(not_5_out), .out(multiplexer_2_out), .sel(in_2),
    .en(arithmatic));
  assign and_1_out = controlled_buffer_2_out & controlled_buffer_1_out;  // AND_Gate and_1, 4 bits wide
  not not_4 (not_4_out, in_1[2]);
  not not_5 (not_5_out, 1'b0);
  Adder #(.width(1)) adder_2 (
    .a(multiplexer_2_out), .b(a0a1a2a3[1]), .out(out_arit_o0o1o2o3[1]), .cin(adder_3_cout),
    .cout(adder_2_cout));
  not not_6 (not_6_out, in_1[1]);
  Multiplexer #(.select(2)) multiplexer_3 (
    .in0(in_1[1]), .in1(not_6_out), .in2(1'b0), .in3(not_7_out), .out(multiplexer_3_out), .sel(in_2),
    .en(arithmatic));
  Adder #(.width(1)) adder_3 (
    .a(multiplexer_3_out), .b(a0a1a2a3[2]), .out(out_arit_o0o1o2o3[2]), .cin(adder_4_cout),
    .cout(adder_3_cout));
  Multiplexer #(.select(2), .width(4)) multiplexer_4 (
    .in0(or_1_out), .in1(and_1_out), .in2(xor_1_out), .in3(not_3_out), .out(out_logical), .sel(in_5));  // open: en
  not not_7 (not_7_out, 1'b0);
  not not_8 (not_8_out, in_1[0]);
  Multiplexer #(.select(2)) multiplexer_5 (
    .in0(in_1[0]), .in1(not_8_out), .in2(1'b0), .in3(not_9_out), .out(multiplexer_5_out), .sel(in_2),
    .en(arithmatic));
  not not_9 (not_9_out, 1'b0);
  Adder #(.width(1)) adder_4 (
    .a(multiplexer_5_out), .b(a0a1a2a3[3]), .out(out_arit_o0o1o2o3[3]), .cin(xor_2_out), .cout(adder_4_cout));
  xor xor_2 (xor_2_out, in_2[0], in_2[1]);
  assign controlled_buffer_2_out = logical ? a0a1a2a3 : 4'bz;  // Controlled_Buffer controlled_buffer_2

  // Other names for the same wires on the sheet: b0 = in_1[0]; b1 = in_1[1]; b2 = in_1[2]; b3 = in_1[3]
endmodule
