// Logisim project fetch_cycle.circ as structural Verilog: 1 circuit, main circuit main
module main (
);

  wire clock_1_out, counter_1_q, decoder_1_out0;
  wire [2:0] decoder_1_out1;
  wire [15:0] adder_1_out, mux_out, Pc_out, ram_1_data, register_1_q, register_3_q;

  Clock clock_1 (.out(clock_1_out));
  Decoder #(.enable("false")) decoder_1 (.out0(decoder_1_out0), .out1(decoder_1_out1[0]), .sel(counter_1_q));
  Counter #(.width(1), .max('h1)) counter_1 (.Q(counter_1_q), .clk(clock_1_out));  // open: load, D, count, carry, clr
  Adder #(.width(16)) adder_1 (.a(Pc_out), .b(16'h1), .out(adder_1_out));  // open: cin, cout
  Register #(.width(16)) register_1 (
    .D(mux_out), .en(decoder_1_out0), .Q(register_1_q), .clk(clock_1_out));  // open: clr
  Register #(.width(16)) register_2 (
    .D(adder_1_out), .en(decoder_1_out1[0]), .Q(Pc_out), .clk(clock_1_out));  // open: clr
  Register #(.width(16)) register_3 (
    .D(mux_out), .en(decoder_1_out1[0]), .Q(register_3_q), .clk(clock_1_out));  // open: clr
  RAM #(.addrWidth(16), .dataWidth(16)) ram_1 (.addr(register_1_q), .data(ram_1_data));  // open: sel, clk, ld, clr
  buf or_1 (decoder_1_out1[2], decoder_1_out1[0]);  // OR_Gate
  or or_2 (decoder_1_out1[1], decoder_1_out1[0], decoder_1_out0);
  Multiplexer #(.select(3), .width(16), .enable("false")) multiplexer_1 (
    .in1(register_1_q), .in2(Pc_out), .in3(register_3_q), .in7(ram_1_data), .out(mux_out),
    .sel(decoder_1_out1));  // open: in0, in4, in5, in6

  // Notes on the sheet:
  //   T0
  //   T1
  //   AR
  //   PC
  //   IR
  //   Memory
endmodule
