// Logisim project fetch_cycle_rkb.circ as structural Verilog: 1 circuit, main circuit main
module main (
);

  wire clock_1_out, decoder_1_out0, decoder_1_out1, decoder_1_out2, decoder_1_out3, or_1_out;
  wire [1:0] counter_1_q;
  wire [11:0] adder_1_out, AR_q, controlled_buffer_1_out, controlled_buffer_2_out, PC_q;
  wire [15:0] controlled_buffer_4_out, IR_q, ram_1_data;

  Clock clock_1 (.out(clock_1_out));
  assign controlled_buffer_1_out = decoder_1_out0 ? PC_q : 12'bz;  // Controlled_Buffer controlled_buffer_1
  Adder #(.width(12)) adder_1 (.a(12'h1), .b(controlled_buffer_2_out), .out(adder_1_out));  // open: cin, cout
  Counter #(.width(2), .max('h3)) counter_1 (.Q(counter_1_q), .clk(clock_1_out));  // open: load, D, count, carry, clr
  Decoder #(.select(2)) decoder_1 (
    .out0(decoder_1_out0), .out1(decoder_1_out1), .out2(decoder_1_out2), .out3(decoder_1_out3),
    .sel(counter_1_q));  // open: en
  Register #(.width(12)) AR (
    .D(controlled_buffer_1_out), .en(decoder_1_out0), .Q(AR_q), .clk(clock_1_out));  // open: clr
  Register #(.width(12)) PC (.D(adder_1_out), .en(decoder_1_out0), .Q(PC_q), .clk(clock_1_out));  // open: clr
  assign controlled_buffer_2_out = decoder_1_out0 ? PC_q : 12'bz;  // Controlled_Buffer controlled_buffer_2
  assign controlled_buffer_1_out = decoder_1_out3 ? controlled_buffer_4_out[11:0] : 12'bz;  // Controlled_Buffer controlled_buffer_3
  RAM #(.addrWidth(12), .dataWidth(16)) ram_1 (.addr(AR_q), .data(ram_1_data));  // open: sel, clk, ld, clr
  Register #(.width(16)) IR (.D(ram_1_data), .en(or_1_out), .Q(IR_q), .clk(clock_1_out));  // open: clr
  or or_1 (or_1_out, decoder_1_out1, decoder_1_out2);
  assign controlled_buffer_4_out = decoder_1_out3 ? IR_q : 16'bz;  // Controlled_Buffer controlled_buffer_4
  Decoder #(.select(3)) decoder_2 (.sel(controlled_buffer_4_out[14:12]));  // open: out0, out1, out2, out3, out4, out5, out6, out7, en
  Register #(.width(1)) register_1 (
    .D(controlled_buffer_4_out[15]), .en(decoder_1_out3), .clk(clock_1_out));  // open: Q, clr
endmodule
