// Logisim project harushicalc.circ as structural Verilog: 1 circuit, main circuit main
module main (
);

  wire _0, _1, _2, _3, _4, _5, _6, _7, _8, _9, and_1_out, and_2_out, and_3_out, and_4_out, and_5_out,
       and_6_out, and_7_out, and_8_out, Clear, or_1_out, or_2_out, or_3_out, or_4_out, or_5_out, or_6_out,
       or_7_out, or_8_out, or_9_out, or_10_out, or_11_out, or_12_out, t_ff_1_qn, t_ff_2_qn, t_ff_3_qn,
       t_ff_4_qn;
  wire [3:0] digit;

  or or_1 (or_1_out, _0, _1, _2, _3, Clear, _4, _5, _6, _7);
  or or_2 (or_2_out, _8, _9);
  or or_3 (or_3_out, _0, _1, Clear, _2, _3, _8, _9);
  or or_4 (or_4_out, _4, _5, _6, _7);
  or or_5 (or_5_out, _0, _1, Clear, _4, _5, _8, _9);
  or or_6 (or_6_out, _2, _3, _6, _7);
  or or_7 (or_7_out, _0, _2, _4, _6, _8, Clear);
  and and_1 (and_1_out, digit[3], or_1_out);
  and and_2 (and_2_out, or_2_out, t_ff_1_qn);
  and and_3 (and_3_out, digit[2], or_3_out);
  and and_4 (and_4_out, or_4_out, t_ff_2_qn);
  and and_5 (and_5_out, digit[1], or_5_out);
  and and_6 (and_6_out, or_6_out, t_ff_3_qn);
  and and_7 (and_7_out, digit[0], or_7_out);
  and and_8 (and_8_out, or_8_out, t_ff_4_qn);
  or or_8 (or_8_out, _1, _3, _5, _7, _9);
  T_Flip_Flop t_ff_1 (.clk(or_9_out), .T(1'b1), .Q(digit[3]), .Qn(t_ff_1_qn));  // open: preset, reset, en
  or or_9 (or_9_out, and_1_out, and_2_out);
  T_Flip_Flop t_ff_2 (.clk(or_10_out), .T(1'b1), .Q(digit[2]), .Qn(t_ff_2_qn));  // open: preset, reset, en
  or or_10 (or_10_out, and_3_out, and_4_out);
  or or_11 (or_11_out, and_5_out, and_6_out);
  T_Flip_Flop t_ff_3 (.clk(or_11_out), .T(1'b1), .Q(digit[1]), .Qn(t_ff_3_qn));  // open: preset, reset, en
  T_Flip_Flop t_ff_4 (.clk(or_12_out), .T(1'b1), .Q(digit[0]), .Qn(t_ff_4_qn));  // open: preset, reset, en
  or or_12 (or_12_out, and_7_out, and_8_out);
  Hex_Digit_Display hex_digit_display_1 (.value(digit));  // open: dp
  Hex_Digit_Display hex_digit_display_2 (.value(digit));  // open: dp
  Hex_Digit_Display hex_digit_display_3 (.value(digit));  // open: dp
  Button u__0 (.out(_0));
  Button u__1 (.out(_1));
  Button u__2 (.out(_2));
  Button u__3 (.out(_3));
  Button u__4 (.out(_4));
  Button u__5 (.out(_5));
  Button u__6 (.out(_6));
  Button u__7 (.out(_7));
  Button u__8 (.out(_8));
  Button u__9 (.out(_9));
  Button CE (.out(Clear));
  Hex_Digit_Display hex_digit_display_4 (.value(digit));  // open: dp
  Hex_Digit_Display hex_digit_display_5 (.value(digit));  // open: dp

  // Notes on the sheet:
  //   Simple calc display with same 5 led output
  //   bit 3
  //   bit2
  //   bit 1
  //   bit0
endmodule
