// Logisim project incr_decr_rkb.circ as structural Verilog: 1 circuit, main circuit main
module main (
  input  in_1,
  input  in_2,
  input  in_3,
  input  in_4,
  input  in_5,
  output out_6,
  output out_7,
  output out_8,
  output out_9,
  output out_10
);

  wire adder_1_cout, adder_2_cout, adder_3_cout, not_1_out;

  not not_1 (not_1_out, in_1);
  Adder #(.width(1)) adder_1 (.a(in_1), .b(in_2), .out(out_9), .cin(not_1_out), .cout(adder_1_cout));
  Adder #(.width(1)) adder_2 (.a(in_1), .b(in_3), .out(out_6), .cin(adder_1_cout), .cout(adder_2_cout));
  Adder #(.width(1)) adder_3 (.a(in_1), .b(in_4), .out(out_7), .cin(adder_2_cout), .cout(adder_3_cout));
  Adder #(.width(1)) adder_4 (.a(in_1), .b(in_5), .out(out_8), .cin(adder_3_cout), .cout(out_10));

  // Notes on the sheet:
  //   <___________________
endmodule
