// Logisim project parallel_bus_tristate_rkb.circ as structural Verilog: 1 circuit, main circuit main
module main (
  input  [1:0] in_1,
  input  [1:0] in_2
);

  wire a, b, c, clock_1_out, d, w, x, y, z;
  wire [3:0] controlled_buffer_1_out, register_1_q, register_2_q, register_3_q, register_4_q;

  Register #(.width(4)) register_1 (
    .D(controlled_buffer_1_out), .en(a), .Q(register_1_q), .clk(clock_1_out));  // open: clr
  assign controlled_buffer_1_out = w ? register_1_q : 4'bz;  // Controlled_Buffer controlled_buffer_1
  Register #(.width(4)) register_2 (
    .D(controlled_buffer_1_out), .en(b), .Q(register_2_q), .clk(clock_1_out));  // open: clr
  assign controlled_buffer_1_out = x ? register_2_q : 4'bz;  // Controlled_Buffer controlled_buffer_2
  Register #(.width(4)) register_3 (
    .D(controlled_buffer_1_out), .en(c), .Q(register_3_q), .clk(clock_1_out));  // open: clr
  assign controlled_buffer_1_out = y ? register_3_q : 4'bz;  // Controlled_Buffer controlled_buffer_3
  Register #(.width(4)) register_4 (
    .D(controlled_buffer_1_out), .en(d), .Q(register_4_q), .clk(clock_1_out));  // open: clr
  assign controlled_buffer_1_out = z ? register_4_q : 4'bz;  // Controlled_Buffer controlled_buffer_4
  Decoder #(.select(2)) decoder_1 (.out0(a), .out1(b), .out2(c), .out3(d), .sel(in_1));  // open: en
  Clock clock_1 (.out(clock_1_out));
  Decoder #(.select(2)) decoder_2 (.out0(w), .out1(x), .out2(y), .out3(z), .sel(in_2));  // open: en

  // Notes on the sheet:
  //   TO
  //   FROM
endmodule
