// Logisim project parralel_bus_rkb.circ as structural Verilog: 1 circuit, main circuit main
module main (
  input  [1:0] in_1,
  input  [1:0] in_2
);

  wire a, b, c, clock_1_out, d;
  wire [3:0] multiplexer_1_out, register_1_q, register_2_q, register_3_q, register_4_q;

  Register #(.width(4)) register_1 (.D(multiplexer_1_out), .en(a), .Q(register_1_q), .clk(clock_1_out));  // open: clr
  Register #(.width(4)) register_2 (.D(multiplexer_1_out), .en(b), .Q(register_2_q), .clk(clock_1_out));  // open: clr
  Multiplexer #(.select(2), .width(4)) multiplexer_1 (
    .in0(register_1_q), .in1(register_2_q), .in2(register_3_q), .in3(register_4_q), .out(multiplexer_1_out),
    .sel(in_2));  // open: en
  Register #(.width(4)) register_3 (.D(multiplexer_1_out), .en(c), .Q(register_3_q), .clk(clock_1_out));  // open: clr
  Register #(.width(4)) register_4 (.D(multiplexer_1_out), .en(d), .Q(register_4_q), .clk(clock_1_out));  // open: clr
  Decoder #(.select(2)) decoder_1 (.out0(a), .out1(b), .out2(c), .out3(d), .sel(in_1));  // open: en
  Clock clock_1 (.out(clock_1_out));
endmodule
