// Logisim project practical_5.circ as structural Verilog: 2 circuits, main circuit main
module main (
  input  [3:0] in_1,
  input  [3:0] in_2,
  input  in_3,
  input  in_4,
  output [3:0] out_5
);

  wire _0, _1, _2, _3, _4, _5, _6, _7, _8, _9, _10, _11, bit_0, bit_1, bit_2, bit_3, d_ff_5_qn,
       decoder_1_out0, decoder_1_out1, decoder_1_out2, decoder_1_out3, decoder_1_out4, decoder_1_out5,
       decoder_1_out6, decoder_1_out7, load_A, load_A_ON, multiplexer_1_out, multiplexer_3_out,
       multiplexer_4_out, multiplexer_5_out, multiplexer_6_out, multiplexer_7_out, multiplexer_8_out,
       multiplexer_9_out, Mux_enable, not_2_out, not_4_out, or_7_out, or_8_out, xor_1_out;
  wire [3:0] adder_1_out, and_1_out, controlled_buffer_1_out, multiplexer_2_out, not_1_out, not_3_out,
       or_2_out, or_3_out, select, xor_2_out;

  Button button_1 (.out(_0));
  Button button_2 (.out(_1));
  Button button_3 (.out(_2));
  Button button_4 (.out(_3));
  Hex_Digit_Display hex_digit_display_1 (.value(select));  // open: dp
  Decoder #(.select(3), .enable("false")) decoder_1 (
    .out0(decoder_1_out0), .out1(decoder_1_out1), .out2(decoder_1_out2), .out3(decoder_1_out3),
    .out4(decoder_1_out4), .out5(decoder_1_out5), .out6(decoder_1_out6), .out7(decoder_1_out7),
    .sel(select[2:0]));
  assign not_1_out = ~in_2;  // NOT_Gate not_1, 4 bits wide
  or or_1 (Mux_enable, decoder_1_out0, decoder_1_out1, decoder_1_out2, decoder_1_out3);
  Multiplexer #(.select(2)) multiplexer_1 (
    .in0(bit_2), .in1(bit_2), .in2(bit_0), .in3(in_4), .out(multiplexer_1_out), .sel(select[1:0]),
    .en(select[3]));
  Button button_5 (.out(_4));
  Button button_6 (.out(_5));
  Button button_7 (.out(_6));
  Button button_8 (.out(_7));
  Multiplexer #(.select(2), .width(4)) multiplexer_2 (
    .in0(in_2), .in1(4'b0000), .in2(not_1_out), .in3(4'b1111), .out(multiplexer_2_out), .sel(select[1:0]),
    .en(Mux_enable));
  Multiplexer multiplexer_3 (
    .in0(in_1[3]), .in1(multiplexer_1_out), .out(multiplexer_3_out), .sel(d_ff_5_qn));  // open: en
  ExactlyOne xor_1 (.out(xor_1_out), .in0(select[0]), .in1(select[1]), .in2(select[2]));
  Adder #(.width(4)) adder_1 (.a(in_1), .b(multiplexer_2_out), .out(adder_1_out), .cin(xor_1_out));  // open: cout
  D_Flip_Flop d_ff_1 (.clk(or_8_out), .D(multiplexer_3_out), .Q(bit_3));  // open: Qn, preset, en, reset
  Button button_9 (.out(_8));
  Button button_10 (.out(_9));
  Button button_11 (.out(_10));
  Button button_12 (.out(_11));
  Button button_13 (.out(load_A));
  LED led_1 (.in(load_A_ON));
  Multiplexer #(.select(2)) multiplexer_4 (
    .in0(bit_1), .in1(bit_1), .in2(bit_3), .in3(bit_3), .out(multiplexer_4_out), .sel(select[1:0]),
    .en(select[3]));
  assign controlled_buffer_1_out = not_2_out ? adder_1_out : 4'bz;  // Controlled_Buffer controlled_buffer_1
  not not_2 (not_2_out, select[2]);
  assign controlled_buffer_1_out = decoder_1_out4 ? and_1_out : 4'bz;  // Controlled_Buffer controlled_buffer_2
  assign and_1_out = in_2 & in_1;  // AND_Gate and_1, 4 bits wide
  assign controlled_buffer_1_out = decoder_1_out5 ? or_2_out : 4'bz;  // Controlled_Buffer controlled_buffer_3
  assign or_2_out = in_2 | in_1;  // OR_Gate or_2, 4 bits wide
  Multiplexer multiplexer_5 (
    .in0(in_1[2]), .in1(multiplexer_4_out), .out(multiplexer_5_out), .sel(d_ff_5_qn));  // open: en
  Hex_Digit_Display hex_digit_display_2 (.value(in_1));  // open: dp
  assign not_3_out = ~in_1;  // NOT_Gate not_3, 4 bits wide
  D_Flip_Flop d_ff_2 (.clk(or_8_out), .D(multiplexer_5_out), .Q(bit_2));  // open: Qn, preset, en, reset
  Hex_Digit_Display hex_digit_display_3 (.value(out_5));  // open: dp
  assign controlled_buffer_1_out = decoder_1_out6 ? xor_2_out : 4'bz;  // Controlled_Buffer controlled_buffer_4
  assign xor_2_out = in_2 ^ in_1;  // XOR_Gate xor_2, 4 bits wide
  assign controlled_buffer_1_out = decoder_1_out7 ? not_3_out : 4'bz;  // Controlled_Buffer controlled_buffer_5
  Multiplexer #(.select(2)) multiplexer_6 (
    .in0(bit_0), .in1(bit_0), .in2(bit_2), .in3(bit_2), .out(multiplexer_6_out), .sel(select[1:0]),
    .en(select[3]));
  Hex_Digit_Display hex_digit_display_4 (.value(in_2));  // open: dp
  Multiplexer multiplexer_7 (
    .in0(in_1[1]), .in1(multiplexer_6_out), .out(multiplexer_7_out), .sel(d_ff_5_qn));  // open: en
  not not_4 (not_4_out, select[3]);
  D_Flip_Flop d_ff_3 (.clk(or_8_out), .D(multiplexer_7_out), .Q(bit_1));  // open: Qn, preset, en, reset
  or or_3 (or_3_out[0], _1, _9, _3, _5, _11, _7);
  or or_4 (or_3_out[1], _2, _10, _3, _6, _11, _7);
  or or_5 (or_3_out[2], _4, _5, _6, _7);
  or or_6 (or_3_out[3], _8, _9, _10, _11);
  assign out_5 = not_4_out ? controlled_buffer_1_out : 4'bz;  // Controlled_Buffer controlled_buffer_6
  assign out_5 = select[3] ? {bit_3, bit_2, bit_1, bit_0} : 4'bz;  // Controlled_Buffer controlled_buffer_7
  Register #(.width(4)) register_1 (.D(or_3_out), .Q(select), .clk(or_7_out));  // open: en, clr
  or or_7 (or_7_out, _0, _1, _2, _3, _4, _5, _6, _7, _8, _9, _10, _11);
  Multiplexer multiplexer_8 (
    .in0(in_1[0]), .in1(multiplexer_9_out), .out(multiplexer_8_out), .sel(d_ff_5_qn));  // open: en
  Multiplexer #(.select(2)) multiplexer_9 (
    .in0(in_3), .in1(bit_3), .in2(bit_1), .in3(bit_1), .out(multiplexer_9_out), .sel(select[1:0]),
    .en(select[3]));
  D_Flip_Flop d_ff_4 (.clk(or_8_out), .D(multiplexer_8_out), .Q(bit_0));  // open: Qn, preset, en, reset
  or or_8 (or_8_out, _8, _9, _10, _11);
  D_Flip_Flop d_ff_5 (.clk(load_A), .D(d_ff_5_qn), .Q(load_A_ON), .Qn(d_ff_5_qn));  // open: preset, en, reset

  // Other names for the same wires on the sheet: A[3:0] = in_1; Ans[3:0] = out_5; B[3:0] = in_2;
  //   select_1[2:0] = select[2:0]

  // Notes on the sheet:
  //   OPERATION
  //   A+B
  //   A+1
  //   A-B
  //   A-1
  //   A'
  //   A and B
  //   A or B
  //   A xor B
  //   SHL
  //   CIL
  //   CIR
  //   SHR
  //   loads reg for shift
  //   INPUT-A
  //   ANSWER
  //   INPUT-B
endmodule

module harshil_unit (
);

  main main_1 ();  // open: in_1, in_2, out_5, in_3, in_4
endmodule
