// Logisim project serial_bus_rkb.circ as structural Verilog: 1 circuit, main circuit main
module main (
  input  [1:0] in_1,
  input  [1:0] in_2
);

  wire a, b, c, clock_1_out, d, multiplexer_1_out, multiplexer_2_out, multiplexer_3_out, multiplexer_4_out,
       multiplexer_5_out, or_1_out, or_2_out, or_3_out, or_4_out, shift_register_1_out, shift_register_2_out,
       shift_register_3_out, shift_register_4_out, w, x, y, z;

  or or_1 (or_1_out, a, w);
  Multiplexer multiplexer_1 (
    .in0(multiplexer_3_out), .in1(shift_register_1_out), .out(multiplexer_1_out), .sel(w));  // open: en
  Shift_Register #(.length(4)) shift_register_1 (
    .shift(or_1_out), .in(multiplexer_1_out), .clk(clock_1_out), .out(shift_register_1_out));  // open: load, clr, d0, q0, d1, q1, d2, q2, d3, q3
  or or_2 (or_2_out, b, x);
  Multiplexer multiplexer_2 (
    .in0(multiplexer_3_out), .in1(shift_register_2_out), .out(multiplexer_2_out), .sel(x));  // open: en
  Shift_Register #(.length(4)) shift_register_2 (
    .shift(or_2_out), .in(multiplexer_2_out), .clk(clock_1_out), .out(shift_register_2_out));  // open: load, clr, d0, q0, d1, q1, d2, q2, d3, q3
  Multiplexer #(.select(2)) multiplexer_3 (
    .in0(shift_register_1_out), .in1(shift_register_2_out), .in2(shift_register_3_out),
    .in3(shift_register_4_out), .out(multiplexer_3_out), .sel(in_2));  // open: en
  or or_3 (or_3_out, c, y);
  Multiplexer multiplexer_4 (
    .in0(multiplexer_3_out), .in1(shift_register_3_out), .out(multiplexer_4_out), .sel(y));  // open: en
  Shift_Register #(.length(4)) shift_register_3 (
    .shift(or_3_out), .in(multiplexer_4_out), .clk(clock_1_out), .out(shift_register_3_out));  // open: load, clr, d0, q0, d1, q1, d2, q2, d3, q3
  Multiplexer multiplexer_5 (
    .in0(multiplexer_3_out), .in1(shift_register_4_out), .out(multiplexer_5_out), .sel(z));  // open: en
  or or_4 (or_4_out, d, z);
  Shift_Register #(.length(4)) shift_register_4 (
    .shift(or_4_out), .in(multiplexer_5_out), .clk(clock_1_out), .out(shift_register_4_out));  // open: load, clr, d0, q0, d1, q1, d2, q2, d3, q3
  Decoder #(.select(2)) decoder_1 (.out0(a), .out1(b), .out2(c), .out3(d), .sel(in_1));  // open: en
  Clock clock_1 (.out(clock_1_out));
  Decoder #(.select(2)) decoder_2 (.out0(w), .out1(x), .out2(y), .out3(z), .sel(in_2));  // open: en

  // Notes on the sheet:
  //   TO
  //   FROM
endmodule
