// Logisim project shifting operations .circ as structural Verilog: 1 circuit, main circuit main
module main (
  input  in_1,
  input  in_2,
  input  in_3,
  input  in_4,
  input  in_5,
  input  in_6,
  input  [2:0] in_7,
  output out_8,
  output out_9,
  output out_10,
  output out_11
);

  wire clock_1_out, multiplexer_1_out, multiplexer_2_out, multiplexer_3_out, multiplexer_4_out;

  Multiplexer #(.select(3)) multiplexer_1 (
    .in0(in_2), .in1(in_5), .in2(in_4), .in3(in_4), .in4(in_2), .in5(in_1), .in6(in_4), .in7(in_4),
    .out(multiplexer_1_out), .sel(in_7));  // open: en
  D_Flip_Flop d_ff_1 (.clk(clock_1_out), .D(multiplexer_1_out), .Q(out_8));  // open: Qn, preset, en, reset
  Multiplexer #(.select(3)) multiplexer_2 (
    .in0(in_3), .in1(in_4), .in2(in_4), .in3(in_3), .in4(in_3), .in5(in_4), .in6(in_2), .in7(in_2),
    .out(multiplexer_2_out), .sel(in_7));  // open: en
  D_Flip_Flop d_ff_2 (.clk(clock_1_out), .D(multiplexer_2_out), .Q(out_9));  // open: Qn, preset, en, reset
  Multiplexer #(.select(3)) multiplexer_3 (
    .in0(in_1), .in1(in_2), .in2(in_2), .in3(in_1), .in4(in_1), .in5(in_2), .in6(in_3), .in7(in_3),
    .out(multiplexer_3_out), .sel(in_7));  // open: en
  D_Flip_Flop d_ff_3 (.clk(clock_1_out), .D(multiplexer_3_out), .Q(out_10));  // open: Qn, preset, en, reset
  Multiplexer #(.select(3)) multiplexer_4 (
    .in0(in_6), .in1(in_3), .in2(in_3), .in3(in_6), .in4(in_4), .in5(in_3), .in6(in_1), .in7(in_1),
    .out(multiplexer_4_out), .sel(in_7));  // open: en
  D_Flip_Flop d_ff_4 (.clk(clock_1_out), .D(multiplexer_4_out), .Q(out_11));  // open: Qn, preset, en, reset
  Clock clock_1 (.out(clock_1_out));

  // Other names for the same wires on the sheet: A0 = in_1; A1 = in_3; A2 = in_2; A3 = in_4

  // Notes on the sheet:
  //   000:shift left
  //   001:shift right
  //   011:arithmatic shift left
  //   100:circular shift left
  //   101:circular shift right
  //   110:nop
  //   111:nop
  //   010:arithmatic shift right
endmodule
